# Fritzing sketch ring-slut (saved by Fritzing 0.9.4)
breadboards: 1

parts:
  Part1 = Arduino Nano (Rev3.0)
  OLED1 = OLED 128x64 I2C Monochrome Display
  RE1 = Rotary Encoder [package=THT]
  Part2 = 24 NeoPixel Ring [part_number=1586]

nets:
  GND: Part1.GND, OLED1.GND, RE1.EncoderPinC, RE1.SwitchPinE, Part2.GND
  N1: Part1.D2, RE1.EncoderPinA
  N2: Part1.D3, RE1.EncoderPinB
  N3: Part1.D4, RE1.SwitchrPinD
  N4: Part1.D10, Part2.IN
  VIN: Part1.VIN, Part2.VDD
  5V: Part1.5V, OLED1.VDD
  N5: Part1.A5, OLED1.SCK
  N6: Part1.A4, OLED1.SDA

custom parts:
  Rotary Encoder: Rotary Encoder from ALPSec11e with switch. This version has an alternate (which has been used in boards) pcb footprint from @opera_night in the forums. It is probably the best one to start from to see if you part matches.
  24 NeoPixel Ring: 24 ultra bright smart LED NeoPixels are arranged in a circle with 2.6" (66mm) outer diameter. The rings are 'chainable' - connect the output pin of one to the input pin of another. Use only one microcontroller pin to control as many as you can chain together! Each LED is addressable as the driver chip is inside the LED. Each one has ~18mA constant current drive so the color will be very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
